# Fritzing sketch robot scheme (saved by Fritzing 0.9.3b)

parts:
  Part1 = Arduino Uno (Rev3)
  Raspberry_Pi_2 = Raspberry Pi 3 [part_number=RPI-3-V1.2]  # not connected
  U1 = TRANSCHIPTC5747 [package=camera_sfv24r-2st_2]  # not connected
  hc-sr1 = hc-sr04
  VCC1 = Battery  # not connected
  U2 = Graphical LCD 128x64 [package=1x20]  # not connected
  U3 = Graphical LCD 128x64 [package=1x20]  # not connected
  U4 = MMA_ACCEL_CONNECTOR [package=1x08]  # not connected
  U5 = MMA_ACCEL_CONNECTOR [package=1x08]  # not connected
  IC1 = L293D [package=THT]
  M3 = DC Motor
  M2 = DC Motor
  S1 = Momentary Switch [package=tactile-pth]
  VCC2 = Battery block 9V  # not connected

nets:
  N1: Part1.D8, hc-sr1.Echo
  N2: Part1.D9_PWM, hc-sr1.Trig
  GND: Part1.GND, hc-sr1.GND, IC1.0V
  N3: Part1.D2, IC1.In_3
  N4: Part1.D3_PWM, IC1.In_4
  N5: Part1.D4, IC1.Enable_2
  N6: Part1.D5_PWM, IC1.Enable_1
  N7: Part1.D6_PWM, IC1.In_2
  N8: Part1.D7, IC1.In_1
  N9: Part1.3V3, IC1.+V
  5V: Part1.5V, hc-sr1.VCC, S1.1
  N10: IC1.Out_1_(_Controlled_by_Enable_1_), M3.pin_2
  N11: IC1.Out_2_(_Controlled_by_Enable_1_), M3.pin_1
  N12: IC1.+Vmotor, S1.4
  N13: IC1.Out_3_(_Controlled_by_Enable_2_), M2.pin_1
  N14: IC1.Out_4_(_Controlled_by_Enable_2_), M2.pin_2

notes:
  COMPUTER:
  -Keyboard
  -Display
  Wi-Fi
  Wheel 1
  Wheel 2
  Serwer
  Client
  ROBOT BOARD / FRAME
  Switch
  Motor Driver
  Ultrasonic Sensor
  Rechargeable Battery
  Power Bank
  Pi Camera
  USB
  Camera Port
  by Bartłomiej Borzyszkowski
